# Fritzing sketch smart-outlet (saved by Fritzing 0.9.3b)
circuit board: 8.46667cm x 5.64444cm
breadboards: 1

parts:
  D1 = Diode [package=diode-1n4148]
  R1 = Resistor [tolerance=±5% resistance=100k package=THT]
  C1 = Electrolytic Capacitor [capacitance=1µF package="100 mil [THT, electrolytic]"]
  IC1 = LM741 [part_number=LM741 package=dip08]
  J1 = female pin header, 3 pins [form="♀ (female)"]
  U2 = Voltage Regulator - 3.3V [package="TO220 [THT]"]
  R2 = Resistor [tolerance=±5% resistance=10k package=THT]
  U1 = ESP8266 WiFi Module [part_number=ESP8266]
  Q1 = NPN-Transistor [package="SOT-23 [SMD]"]
  R3 = Resistor [tolerance=±5% resistance=10k package=THT]
  U4 = RELAY [package=relay-jzc]
  D2 = Rectifier Diode [part_number=1N4001 package="300 mil [THT]"]
  L1 = Inductor [package="0805 [SMD]"]
  J2 = Screw terminal - 2 pins [part_number="220V IN" package=THT]
  J3 = Screw terminal - 2 pins [part_number="220V Out" package=THT]
  LED1 = LEDs [package=led10mm]
  R4 = Resistor [tolerance=±5% resistance=6.8k package=THT]

nets (from the schematic view):
  N1: D1.A, IC1.OUTPUT
  N2: D1.C, R1.Pin_1, C1.+, IC1.-INPUT, U1.ADC_0
  GND: R1.Pin_0, C1.-, J1.pin3, U2.GND, U1.GND, Q1.2, R4.Pin_0
  N3: IC1.+OFFSET, IC1.NC
  N4: IC1.+INPUT, J1.pin2
  -5V: IC1.V-
  5V: IC1.V+, J1.pin1, U2.input_voltage, U4.COIL1, D2.cathode
  3.3V: U2.output_voltage, R2.Pin_1, U1.VCC
  N5: R2.Pin_0, U1.CH_PD
  N6: U1.GPIO_0, R3.Pin_0
  N7: U1.GPIO_2, LED1.A
  N8: Q1.0, R3.Pin_1
  N9: Q1.1, U4.COIL2, D2.anode
  N10: U4.NC, J3.pin1
  N11: U4.NO, L1.pin_0
  N12: L1.pin_1, J2.pin2
  N13: J2.pin1, J3.pin2
  N14: LED1.C, R4.Pin_1

custom parts:
  LM741: General Purpose Operational Amplifier
